# Fritzing sketch dls_electronics (saved by Fritzing 0.9.9b)
breadboards: 1

parts:
  15V = Voltage Regulator - 5V [package="TO220 [THT]"]
  12_V = Voltage Regulator - 5V [package="TO220 [THT]"]
  5V = Voltage Regulator - 5V [package="TO220 [THT]"]
  12V_1 = Voltage Regulator - 5V [package="TO220 [THT]"]
  Power_plug1 = Power plug
  DAQ_pico_(representation) = Arduino Prototyping Shield
  X2 = USB Connectors [package=usb-a-s-silk-female]
  Composant1 = Arduino Uno (Rev3) - ICSP
  Motor_attenuator_encoder = PHOTOTRANSISTOR REFLECTIVE OBJECT SENSOR [package=qrb1114-side]
  motor_rotation = Stepper Motor - Bipolar
  Encoder_rotation_(wrong_model)_needs_two_more_wire_(GND_+code_sense) = YumoE6B2
  motor_attenuator = Stepper Motor - Bipolar
  R1 = Resistor [tolerance=±5% power=0.25 resistance=390 package=THT]
  R2 = Resistor [tolerance=±5% power=0.25 resistance=100k package=THT]
  L298N1 = L298N DC motor driver
  L298N2 = L298N DC motor driver

nets:
  N1: 15V.input_voltage, 12_V.input_voltage, 5V.input_voltage, 12V_1.input_voltage, Power_plug1.VCC
  GND: 15V.GND, 12_V.GND, 5V.GND, 12V_1.GND, Power_plug1.GND, DAQ_pico_(representation).GND, Composant1.GND, L298N1.GND, L298N2.GND
  N2: 15V.output_voltage, Encoder_rotation_(wrong_model)_needs_two_more_wire_(GND_+code_sense).V
  N3: 12_V.output_voltage, L298N2.12V
  N4: 5V.output_voltage, DAQ_pico_(representation).+5V, Composant1.D0/RX, Motor_attenuator_encoder.C, R1.Pin_0, R2.Pin_1
  N5: 12V_1.output_voltage, Composant1.VIN
  N6: DAQ_pico_(representation).N$321, X2.GND
  N7: DAQ_pico_(representation).N$322, X2.VBUS
  N8: Composant1.D8, L298N1.IN4
  N9: Composant1.D9_PWM, L298N2.IN1
  N10: Composant1.D10_PWM/SS, L298N2.IN2
  N11: Composant1.D11_PWM/MOSI, L298N2.IN3
  N12: Composant1.D12/MISO, L298N2.IN4
  N13: Composant1.D1/TX, Encoder_rotation_(wrong_model)_needs_two_more_wire_(GND_+code_sense).GND
  N14: Composant1.D2, Encoder_rotation_(wrong_model)_needs_two_more_wire_(GND_+code_sense).Z
  N15: Composant1.D3_PWM, Encoder_rotation_(wrong_model)_needs_two_more_wire_(GND_+code_sense).B
  N16: Composant1.D4, Encoder_rotation_(wrong_model)_needs_two_more_wire_(GND_+code_sense).A
  N17: Composant1.D5_PWM, L298N1.IN1
  N18: Composant1.D6_PWM, L298N1.IN2
  N19: Composant1.D7, L298N1.IN3
  5V: Composant1.5V, L298N1.5V, L298N2.5V
  N20: Motor_attenuator_encoder.A, R1.Pin_1
  N21: Motor_attenuator_encoder.E, Motor_attenuator_encoder.K
  N22: motor_rotation.A, L298N2.OUT3
  N23: motor_rotation.C, L298N2.OUT4
  N24: motor_rotation.B, L298N2.OUT2
  N25: motor_rotation.D, L298N2.OUT1
  N26: motor_attenuator.A, L298N1.OUT1
  N27: motor_attenuator.C, L298N1.OUT2
  N28: motor_attenuator.B, L298N1.OUT4
  N29: motor_attenuator.D, L298N1.OUT3

notes:
  PC

custom parts:
  L298N DC motor driver: 2x DC motor driver with 78M05 positive voltage regulator (7..35 V) L298N: max 46 V, 2 A Set 5 V Enable jumper to enable 5 V regultor (needed for the L298N) and +5 V output at screw terminal or supply external +5 V at screw terminal Set ENA and/or ENB to +5 V to enable motor permanently or supply ENA and/or ENB with PWM signal IN1 and IN2 set rotation directory for motor A (OUT1/OUT2) IN2 and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
